// Logisim project afisor_03_ad.circ as structural Verilog
module main (
  input  [2:0] in_1
);

  wire [6:0] afisor_03ad_1_catodes;

  afisor_03ad afisor_03ad_1 (.mode(in_1), .catodes(afisor_03ad_1_catodes));
  _7_Segment_Display u_7_segment_display_1 (
    .g(afisor_03ad_1_catodes[0]), .f(afisor_03ad_1_catodes[1]), .a(afisor_03ad_1_catodes[6]),
    .b(afisor_03ad_1_catodes[5]), .e(afisor_03ad_1_catodes[2]), .d(afisor_03ad_1_catodes[3]),
    .c(afisor_03ad_1_catodes[4]));  // open: dp
endmodule

// VHDL entity afisor_03ad, as the project stores it:
--------------------------------------------------------------------------------
-- Project :
-- File    :
-- Autor   :
-- Date    :
--
--------------------------------------------------------------------------------
-- Description :
--
--------------------------------------------------------------------------------

LIBRARY ieee;
USE ieee.std_logic_1164.all;

ENTITY afisor_03ad IS
  PORT (
  	mode: in std_logic_vector(2 downto 0);
  	catodes: out std_logic_vector(6 downto 0)
    );
END afisor_03ad;

--------------------------------------------------------------------------------
--Complete your VHDL description below
--------------------------------------------------------------------------------

ARCHITECTURE TypeArchitecture OF afisor_03ad IS

BEGIN
	catodes <= "0110000" when mode = "000" else
				"1101101" when mode = "001" else
				"1000000" when mode ="010" else
				"0100000" when mode ="011" else
				"0010000" when mode ="100" else
				"0001000" when mode ="101" else
				"0000100" when mode ="110" else
				"0000010" when mode ="111";

END TypeArchitecture;
