// Logisim project afisor_03_ad_all.circ as structural Verilog
module main (
  output [7:0] ANODES,
  output [6:0] CATODES
);

  wire clock_1_out, clock_div_1_clk_div;
  wire [2:0] decodificator_prioritar_1_outp;

  Clock clock_1 (.out(clock_1_out));
  clock_div clock_div_1 (.clk(clock_1_out), .clk_div(clock_div_1_clk_div));
  ringshifter ringshifter_1 (.clk(clock_div_1_clk_div), .en(1'b1), .outp(ANODES));
  decodificator_prioritar decodificator_prioritar_1 (
    .clk(clock_1_out), .data(ANODES), .outp(decodificator_prioritar_1_outp));
  mux81 mux81_1 (.sel(decodificator_prioritar_1_outp), .outp(CATODES));
endmodule

// VHDL entity afisor_ad03, as the project stores it:
--------------------------------------------------------------------------------
-- Project :
-- File    :
-- Autor   :
-- Date    :
--
--------------------------------------------------------------------------------
-- Description :
--
--------------------------------------------------------------------------------

LIBRARY ieee;
USE ieee.std_logic_1164.all;

ENTITY afisor_ad03 IS
  PORT (
  ------------------------------------------------------------------------------
  --Insert input ports below
    clock      : IN  std_logic;                    -- input bit example
    val        : IN  std_logic_vector(3 DOWNTO 0); -- input vector example
  ------------------------------------------------------------------------------
  --Insert output ports below
    max        : OUT std_logic;                    -- output bit example
    cpt        : OUT std_logic_vector(3 DOWNTO 0)  -- output vector example
    );
END afisor_ad03;

--------------------------------------------------------------------------------
--Complete your VHDL description below
--------------------------------------------------------------------------------

ARCHITECTURE TypeArchitecture OF afisor_ad03 IS

BEGIN


END TypeArchitecture;

// VHDL entity mux81, as the project stores it:
--------------------------------------------------------------------------------
-- Project :
-- File    :
-- Autor   :
-- Date    :
--
--------------------------------------------------------------------------------
-- Description :
--
--------------------------------------------------------------------------------

LIBRARY ieee;
USE ieee.std_logic_1164.all;

ENTITY mux81 IS
  PORT (
	sel: in std_logic_vector(2 downto 0);
	outp: out std_logic_vector(6 downto 0)
    );
END mux81;

--------------------------------------------------------------------------------
--Complete your VHDL description below
--------------------------------------------------------------------------------

ARCHITECTURE TypeArchitecture OF mux81 IS

BEGIN
	outp <= 	"0000001" when sel = "000" else
			"0000010" when sel = "001" else
			"0000100" when sel = "010" else
			"0011010" when sel = "011" else
			"0010000" when sel = "100" else
			"0100000" when sel = "101" else
			"1000000" when sel = "110" else
			"1000001" when sel = "111";
END TypeArchitecture;

// VHDL entity ringshifter, as the project stores it:
--------------------------------------------------------------------------------
-- Project :
-- File    :
-- Autor   :
-- Date    :
--
--------------------------------------------------------------------------------
-- Description :
--
--------------------------------------------------------------------------------

LIBRARY ieee;
USE ieee.std_logic_1164.all;

ENTITY ringshifter IS
  PORT (
	clk, en: in std_logic;
	outp: out std_logic_vector(7 downto 0)
    );
END ringshifter;

--------------------------------------------------------------------------------
--Complete your VHDL description below
--------------------------------------------------------------------------------

ARCHITECTURE TypeArchitecture OF ringshifter IS
signal ring : std_logic_vector(7 downto 0) := "00000001";
signal temp_ring : std_logic_vector(7 downto 0);
BEGIN
	process(clk)
	begin
		if en = '0' then
			temp_ring <= "00000001";
		elsif rising_edge(clk) then
			ring <= ring(0) & ring(7 downto 1);
			temp_ring <= ring;
			
		end if;
		outp <= temp_ring;
	end process;

END TypeArchitecture;

// VHDL entity clock_div, as the project stores it:
--------------------------------------------------------------------------------
-- Project :
-- File    :
-- Autor   :
-- Date    :
--
--------------------------------------------------------------------------------
-- Description :
--
--------------------------------------------------------------------------------

LIBRARY ieee;
USE ieee.std_logic_1164.all;
use ieee.std_logic_unsigned.all;

ENTITY clock_div IS
  PORT (
	clk : in std_logic;
	clk_div : out std_logic
    );
END clock_div;

--------------------------------------------------------------------------------
--Complete your VHDL description below
--------------------------------------------------------------------------------

ARCHITECTURE TypeArchitecture OF clock_div IS
signal temp : std_logic_Vector(16 downto 0);
BEGIN
	process(clk) 
	begin
		if rising_edge(clk) then
			temp <= temp + 1;
			clk_div <= temp(16);
		end if;
	end process;

END TypeArchitecture;

// VHDL entity decodificator_prioritar, as the project stores it:
--------------------------------------------------------------------------------
-- Project :
-- File    :
-- Autor   :
-- Date    :
--
--------------------------------------------------------------------------------
-- Description :
--
--------------------------------------------------------------------------------

LIBRARY ieee;
USE ieee.std_logic_1164.all;

ENTITY decodificator_prioritar IS
  PORT (
	clk: in std_logic;
	data : in std_logic_vector(7 downto 0);
	outp: out std_logic_vector(2 downto 0)
    );
END decodificator_prioritar;

--------------------------------------------------------------------------------
--Complete your VHDL description below
--------------------------------------------------------------------------------

ARCHITECTURE TypeArchitecture OF decodificator_prioritar IS

BEGIN
	outp <= 	"000" when data(0) = '1' else
			"001" when data(1) = '1' else
			"010" when data(2) = '1' else
			"011" when data(3) = '1' else
			"100" when data(4) = '1' else
			"101" when data(5) = '1' else
			"110" when data(6) = '1' else
			"111" when data(7) = '1';

END TypeArchitecture;
