// Logisim project bcd_to_zec_flux.circ as structural Verilog
module main (
  input  [3:0] in_1,
  output [9:0] out_2
);

  bcd_to_zec bcd_to_zec_1 (.\input (in_1), .\output (out_2));
endmodule

// VHDL entity bcd_to_zec, as the project stores it:
LIBRARY ieee;
USE ieee.std_logic_1164.all;
use ieee.std_logic_unsigned.all;

ENTITY bcd_to_zec IS
  PORT (
	input : in std_logic_vector(3 downto 0);
	output: out std_logic_vector(9 downto 0)
    );
END bcd_to_zec;

--------------------------------------------------------------------------------
--Complete your VHDL description below
--------------------------------------------------------------------------------

ARCHITECTURE TypeArchitecture OF bcd_to_zec IS

BEGIN
	output(0) <= not input(3) and not input (2) and not input(1) and not input(0);
	output(1) <= not input(3) and not input (2) and not input(1) and input(0);
	output(2) <= not input(3) and not input (2) and input(1) and not input(0);
	output(3) <= not input(3) and not input (2) and input(1) and input(0);
	--etc.

END TypeArchitecture;

--0000 1000000000
--0001 0100000000
--0010 0010000000
--0011 0001000000
--0100 0000100000
--0101
--0110
--0111
--1000
--1001
