// Logisim project codificatoare.circ as structural Verilog
module main (
  input  [3:0] in_1,
  output [3:0] out_2
);

  bcd_to_gray bcd_to_gray_1 (.bcd(in_1), .gray(out_2));
endmodule

// VHDL entity bcd_to_gray, as the project stores it:
LIBRARY ieee;
USE ieee.std_logic_1164.all;
use ieee.std_logic_unsigned.all;

ENTITY bcd_to_gray IS
  PORT (
  	bcd: in std_logic_vector(3 downto 0);
  	gray: out std_logic_vector(3 downto 0)
	);
END bcd_to_gray;

ARCHITECTURE TypeArchitecture OF bcd_to_gray IS

BEGIN
	gray <= 	"0000" when bcd = "0000" else
			"0001" when bcd = "0001" else
			"0011" when bcd = "0010" else 
			"0010" when bcd = "0011" else 
			"1110" when bcd = "0100" else 
			"1111" when bcd = "0101" else 
			"1101" when bcd = "0110" else 
			"1100" when bcd = "0111" else 
			"1111";

END TypeArchitecture;

// VHDL entity bcd_to_2421, as the project stores it:
LIBRARY ieee;
USE ieee.std_logic_1164.all;

ENTITY bcd_to_2421 IS
  PORT (
	bcd: in std_logic_Vector(3 downto 0);
	outp: out std_logic_vector(3 downto 0)
    );
END bcd_to_2421;

--------------------------------------------------------------------------------
--Complete your VHDL description below
--------------------------------------------------------------------------------

ARCHITECTURE TypeArchitecture OF bcd_to_2421 IS

BEGIN
	outp <= 	"0000" when bcd = "0000" else
			"0001" when bcd = "0001" else
			"0010" when bcd = "0010" else
			"0011" when bcd = "0011" else
			"0100" when bcd = "0100" else
			"1011" when bcd = "0101" else
			"1100" when bcd = "0110" else
			"1101" when bcd = "0111" else
			"1110" when bcd = "1000" else
			"1111" when bcd = "1001" else
			"1111";

END TypeArchitecture;

// VHDL entity exces3_to_bcd, as the project stores it:
LIBRARY ieee;
USE ieee.std_logic_1164.all;

ENTITY exces3_to_bcd IS
  PORT (
	exces3: in std_logic_vector(3 downto 0);
	bcd: out std_logic_vector(3 downto 0)
    );
END exces3_to_bcd;

--------------------------------------------------------------------------------
--Complete your VHDL description below
--------------------------------------------------------------------------------

ARCHITECTURE TypeArchitecture OF exces3_to_bcd IS

BEGIN
	bcd <= 	"0000" when exces3 = "0011" else
			"0001" when exces3 = "0100" else
			"0010" when exces3 = "0101" else
			"0011" when exces3 = "0110" else
			"0100" when exces3 = "0111" else
			"0101" when exces3 = "1000" else
			"0110" when exces3 = "1001" else
			"0111" when exces3 = "1010" else
			"1000" when exces3 = "1011" else
			"1001" when exces3 = "1100" else
			"1111";
			

END TypeArchitecture;

// VHDL entity dec_to_bcd, as the project stores it:
LIBRARY ieee;
USE ieee.std_logic_1164.all;

ENTITY dec_to_bcd IS
  PORT (
	decimal: in std_logic_vector(9 downto 0);
	bcd: out std_logic_vector(3 downto 0)
    );
END dec_to_bcd;

--------------------------------------------------------------------------------
--Complete your VHDL description below
--------------------------------------------------------------------------------

ARCHITECTURE TypeArchitecture OF dec_to_bcd IS

BEGIN
	bcd <= "0000" when decimal(0) = '1' else 
	 "0001" when decimal(1) = '1' else 
	"0010" when decimal(2) = '1' else 
	"0011" when decimal(3) = '1' else 
	 "0100" when decimal(4) = '1' else 
	 "0101" when decimal(5) = '1' else 
	 "0110" when decimal(6) = '1' else 
	 "0111" when decimal(7) = '1' else 
	 "1000" when decimal(8) = '1' else 
	 "1001" when decimal(9) = '1' else 
	"1111"; 

END TypeArchitecture;
