// Logisim project comparator_2bit_structural.circ as structural Verilog
module main (
  input  [1:0] in_1,
  input  [1:0] in_2,
  output out_3,
  output out_4,
  output out_5
);

  comparator_2bit comparator_2bit_1 (.a(in_1), .b(in_2), .mic(out_3), .mare(out_4), .egal(out_5));
endmodule

// VHDL entity comparator_2bit, as the project stores it:
LIBRARY ieee;
USE ieee.std_logic_1164.all;

ENTITY comparator_2bit IS
  PORT (
	a: in std_logic_vector(1 downto 0);
	b: in std_logic_vector(1 downto 0);
	mic, mare, egal: out std_logic
    );
END comparator_2bit;

--e1 and 2e = e
--m1 or (e1 and mic2) = m
--M1 or (e1 and M2) = M
ARCHITECTURE TypeArchitecture OF comparator_2bit IS
component ANDG is
	PORT (
	a,b: in std_logic;
	o: out std_logic
	);
end component;
component ORG is
	PORT (
	a,b: in std_logic;
	o: out std_logic
	);
end component;
component comparator_1bit IS
  PORT (
	a: in std_logic;
	b: in std_logic;
	mic, mare, egal: out std_logic
    );
END component;


signal w1, w2, m1, e1, g1, m2, e2, g2,e,g,m: std_logic;
BEGIN
CMP1: comparator_1bit port map(a(1), b(1), m1, g1, e1);
CMP2: comparator_1bit port map(a(0), b(0), m2, g2, e2);
ANDE: ANDG port map(e1, e2, egal);
AND1: ANDG port map(e1, m2, w1);
AND2: ANDG port map(e1, g2, w2);
OR1: ORG port map(g1,w2, mare);
OR2: ORG port map(m1, w1, mic);

END TypeArchitecture;




LIBRARY ieee;
USE ieee.std_logic_1164.all;
ENTITY ANDG is
	PORT (
	a,b: in std_logic;
	o: out std_logic
	);
end ANDG;

architecture flux of ANDG is
begin
	o <= a and b;
end flux;


LIBRARY ieee;
USE ieee.std_logic_1164.all;
ENTITY ORG is
	PORT (
	a,b: in std_logic;
	o: out std_logic
	);
end ORG;

architecture flux of ORG is
begin
	o <= a or b;
end flux;


LIBRARY ieee;
USE ieee.std_logic_1164.all;

ENTITY comparator_1bit IS
  PORT (
	a: in std_logic;
	b: in std_logic;
	mic, mare, egal: out std_logic
    );
END comparator_1bit;

--e1 and 2e = e
--m1 or (e1 and mic2) = m
--M1 or (e1 and M2) = M
ARCHITECTURE TypeArchitecture OF comparator_1bit IS

BEGIN
	process(a,b) 
	begin
		mic <= '0';
		mare <= '0';
		egal <= '0';
		if a > b then
			mare <= '1';
		elsif a = b then
			egal <= '1';
		else
			mic <= '1';
		end if;
	end process;

END TypeArchitecture;
