// Logisim project counter_sincron.circ as structural Verilog
module main (
  input  in_1,
  input  in_2,
  input  [7:0] in_3,
  output [7:0] out_4
);

  wire clock_1_out;

  Clock clock_1 (.out(clock_1_out));
  counter counter_1 (.clk(clock_1_out), .reset(in_1), .ld(in_2), .data(in_3), .\output (out_4));
endmodule

// VHDL entity counter, as the project stores it:
LIBRARY ieee;
USE ieee.std_logic_1164.all;
use ieee.std_logic_unsigned.all;


ENTITY counter IS
  PORT (
  	clk, reset, ld: in std_logic;
	data: in std_logic_vector(7 downto 0);
	output: out std_logic_vector(7 downto 0)
    );
END counter;

--------------------------------------------------------------------------------
--Complete your VHDL description below
--------------------------------------------------------------------------------

ARCHITECTURE TypeArchitecture OF counter IS
signal number : std_logic_vector(7 downto 0) := "00000000";
BEGIN
	process(clk, reset)
	begin
		if reset = '1' then
			number <= "00000000";
		elsif rising_edge(clk) then
			if ld = '1' then
				number <= data;
			else
				number <= number + 1;
			end if;
		end if;
		output <= number;
	end process;

END TypeArchitecture;
