// Logisim project detector_paritate_4b.circ as structural Verilog
module main (
  input  [3:0] in_1,
  output [4:0] out_2
);

  det_paritate_4b det_paritate_4b_1 (.data(in_1), .outp(out_2));
endmodule

// VHDL entity det_paritate_4b, as the project stores it:
--------------------------------------------------------------------------------
-- Project :
-- File    :
-- Autor   :
-- Date    :
--
--------------------------------------------------------------------------------
-- Description :
--
--------------------------------------------------------------------------------

LIBRARY ieee;
USE ieee.std_logic_1164.all;

ENTITY det_paritate_4b IS
  PORT (
	data: in std_logic_vector(3 downto 0);
	outp: out std_logic_vector(4 downto 0)
    );
END det_paritate_4b;

--------------------------------------------------------------------------------
--Complete your VHDL description below
--------------------------------------------------------------------------------

ARCHITECTURE TypeArchitecture OF det_paritate_4b IS

BEGIN
	process(data)
	variable n : integer := 0;
	begin
	n := 0;
	if data(0) = '1' then
		n := n + 1;
	end if;
	if data(1) = '1' then
		n := n + 1;
	end if;
	if data(2) = '1' then
		n := n + 1;
	end if;
	if data(3) = '1' then
		n := n + 1;
	end if;
	outp(4 downto 1) <= data;

	if n rem 2 = 1 then
		outp(0) <= '1';
	else 
		outp(0) <= '0';
	end if;
	
	end process;
END TypeArchitecture;
