// Logisim project dmux_1to4_concurent.circ as structural Verilog
module main (
  input  in_1,
  input  [1:0] in_2,
  output [3:0] out_3
);

  dmux_1to4 dmux_1to4_1 (.\input (in_1), .sel(in_2), .\output (out_3));
endmodule

// VHDL entity dmux_1to4, as the project stores it:
--------------------------------------------------------------------------------
-- Project :
-- File    :
-- Autor   :
-- Date    :
--
--------------------------------------------------------------------------------
-- Description :
--
--------------------------------------------------------------------------------

LIBRARY ieee;
USE ieee.std_logic_1164.all;

ENTITY dmux_1to4 IS
  PORT (
	input: in std_logic;
	sel: in std_logic_vector(1 downto 0);
	output: out std_logic_vector(3 downto 0)
    );
END dmux_1to4;

--------------------------------------------------------------------------------
--Complete your VHDL description below
--------------------------------------------------------------------------------

ARCHITECTURE TypeArchitecture OF dmux_1to4 IS

BEGIN
	output(0) <= input and not sel(1) and not sel(0);
	output(1) <= input and not sel(1) and sel(0);
	output(2) <= input and sel(1) and not sel(0);
	output(3) <= input and sel(1) and sel(0);

END TypeArchitecture;
