// Logisim project fifo.circ as structural Verilog
module main (
  input  in_1,
  input  in_2,
  input  [3:0] in_3,
  output [3:0] out_4
);

  wire clock_1_out;

  Clock clock_1 (.out(clock_1_out));
  fifo8x4 fifo8x4_1 (.clk(clock_1_out), .push(in_1), .pop(in_2), .data_in(in_3), .data_out(out_4));
endmodule

// VHDL entity fifo8x4, as the project stores it:
--------------------------------------------------------------------------------
-- Project :
-- File    :
-- Autor   :
-- Date    :
--
--------------------------------------------------------------------------------
-- Description :
--
--------------------------------------------------------------------------------

LIBRARY ieee;
USE ieee.std_logic_1164.all;

ENTITY fifo8x4 IS
  PORT (
	clk, push, pop: in std_logic;
	data_in : in std_logic_vector(3 downto 0);
	data_out : out std_logic_vector(3 downto 0)
    );
END fifo8x4;


ARCHITECTURE TypeArchitecture OF fifo8x4 IS
type matrix is array(0 to 7) of std_logic_vector(3 downto 0);
signal memory : matrix := (others => "0000");
BEGIN
	process(clk)
	variable stack_pointer : integer := 0;
	begin
	if rising_edge(clk) then
		if push = '1' then
			stack_pointer := stack_pointer + 1;
			memory(stack_pointer) <= data_in;
		elsif pop = '1' then
			stack_pointer := stack_pointer-1;
			if stack_pointer < 0 then
				stack_pointer := 0;
			end if;
		end if;
		data_out <= memory(stack_pointer);
	end if;
	end process;

END TypeArchitecture;
