// Logisim project jk_sincronn.circ as structural Verilog
module main (
  input  in_1,
  input  in_2,
  input  in_3,
  input  in_4,
  output out_5
);

  wire clock_1_out;

  Clock clock_1 (.out(clock_1_out));
  jk_sincron jk_sincron_1 (.clk(clock_1_out), .j(in_1), .k(in_2), .s(in_3), .r(in_4), .\output (out_5));
endmodule

// VHDL entity jk_sincron, as the project stores it:
--------------------------------------------------------------------------------
-- Project :
-- File    :
-- Autor   :
-- Date    :
--
--------------------------------------------------------------------------------
-- Description :
--
--------------------------------------------------------------------------------

LIBRARY ieee;
USE ieee.std_logic_1164.all;

ENTITY jk_sincron IS
  PORT (
  	clk: in std_logic;
	j,k,s,r: in std_logic;
	output: out std_logic
    );
END jk_sincron;

--------------------------------------------------------------------------------
--Complete your VHDL description below
--------------------------------------------------------------------------------

ARCHITECTURE TypeArchitecture OF jk_sincron IS
signal q: std_logic := '0';
BEGIN
	process(clk)
	begin
		if s = '1' then 
			q <= '1';
		elsif r = '1' then
			q <= '0';
		elsif rising_edge(clk) then
			if j = '1' and k = '1' then
				q <= not q;
			elsif j = '1' then
				q <= '1';
			elsif k = '1' then
				q <= '0';
			end if;
		end if;
		output <= q;
	end process;

END TypeArchitecture;
