// Logisim project lifo.circ as structural Verilog
module main (
  input  in_1,
  input  in_2,
  input  [3:0] in_3,
  output [3:0] out_4
);

  wire clock_1_out;

  Clock clock_1 (.out(clock_1_out));
  lifo8x4 lifo8x4_1 (.clk(clock_1_out), .push(in_1), .pop(in_2), .data_in(in_3), .data_out(out_4));
endmodule

// VHDL entity lifo8x4, as the project stores it:
LIBRARY ieee;
USE ieee.std_logic_1164.all;

ENTITY lifo8x4 IS
  PORT (
	clk,push,pop : in std_logic;
	data_in: in std_logic_vector(3 downto 0);
	data_out: out std_logic_Vector(3 downto 0)
    );
END lifo8x4;


ARCHITECTURE TypeArchitecture OF lifo8x4 IS
type matrix is array(0 to 7) of std_logic_vector(3 downto 0);
signal memory : matrix := (others => "0000");
signal temp : std_logic_vector(3 downto 0) := "0000";
BEGIN
	process(clk)
	variable stack_pointer : integer := 0;
	begin
		if rising_edge(clk) then
			if push = '1' then
				if stack_pointer < 8 then 
					memory(stack_pointer) <= data_in;
				end if;
				stack_pointer := stack_pointer + 1;
				if stack_pointer > 7 then
					stack_pointer := 7;
				end if;
			elsif pop = '1' then
				if stack_pointer = 0 then 
					memory <= memory;
				else
					memory(0 to stack_pointer) <= memory(1 to stack_pointer+1);
				end if;
				stack_pointer := stack_pointer - 1;
				if stack_pointer < 0 then
					stack_pointer := 0;
				end if;
			end if;
			data_out <= memory(0);
		end if;
	
	end process;
END TypeArchitecture;
