// Logisim project moebius_8bit.circ as structural Verilog
module main (
  output [7:0] out_1
);

  wire clock_1_out;

  Clock clock_1 (.out(clock_1_out));
  moebius moebius_1 (.clk(clock_1_out), .q(out_1));
endmodule

// VHDL entity moebius, as the project stores it:
--------------------------------------------------------------------------------
-- Project :
-- File    :
-- Autor   :
-- Date    :
--
--------------------------------------------------------------------------------
-- Description :
--
--------------------------------------------------------------------------------

LIBRARY ieee;
USE ieee.std_logic_1164.all;

ENTITY moebius IS
  PORT (
	clk : in std_logic;
	q: out std_logic_vector(7 downto 0)
    );
END moebius;


ARCHITECTURE TypeArchitecture OF moebius IS
signal number : std_logic_vector(7 downto 0) := "00000000";
BEGIN
	process(clk)
	variable x : std_logic := '0';
	begin
		if rising_edge(clk) then
			x := number(0);
			number(6 downto 0) <= number(7 downto 1);
			number(7) <= not x;
		end if;
		q <= number;
	end process;


END TypeArchitecture;



LIBRARY ieee;
USE ieee.std_logic_1164.all;


entity BISTABIL_D is
	port (
		clk, d, s, r: in std_logic;
		outp: out std_logic
	);
end BISTABIL_D;

architecture Behav of BISTABIL_D is
signal q : std_logic := '0';
begin
	process(clk, s, r)
	begin
		if r = '1' then
			q <= '0';
		elsif s = '1' then
			q <= '1';
		elsif rising_edge(clk) then
			q <= d;
		end if;
		outp <= q;
	end process;
end Behav;
