// Logisim project mram_8x4.circ as structural Verilog
module main (
  input  in_1,
  input  [2:0] in_2,
  input  [3:0] in_3,
  output [3:0] out_4
);

  wire clock_1_out;

  Clock clock_1 (.out(clock_1_out));
  ram_8x4 ram_8x4_1 (.clock(clock_1_out), .we(in_1), .address(in_2), .data(in_3), .outp(out_4));
endmodule

// VHDL entity ram_8x4, as the project stores it:
LIBRARY ieee;
USE ieee.std_logic_1164.all;
use ieee.std_logic_unsigned.all;

ENTITY ram_8x4 IS
  PORT (
	clock: in std_logic;
	we: in std_logic;
	address: in std_logic_vector(2 downto 0);
	data: in std_logic_vector(3 downto 0);
	outp : out std_logic_vector(3 downto 0)
    );
END ram_8x4;

ARCHITECTURE TypeArchitecture OF ram_8x4 IS
type matrix is array(0 to 7) of std_logic_vector(3 downto 0);
signal memory : matrix := (others => "0000");
BEGIN
	process(clock)
	begin
		if rising_edge(clock) then
			if we = '1' then
				memory(conv_integer(address)) <= data;
			end if;
			outp <= memory(conv_integer(address));
		end if;
	end process;


END TypeArchitecture;
