// Logisim project mrom_8x4.circ as structural Verilog
module main (
  input  [2:0] in_1,
  output [3:0] out_2
);

  wire clock_1_out;

  Clock clock_1 (.out(clock_1_out));
  rom_8x4 rom_8x4_1 (.clock(clock_1_out), .address(in_1), .outp(out_2));
endmodule

// VHDL entity rom_8x4, as the project stores it:
--------------------------------------------------------------------------------
-- Project :
-- File    :
-- Autor   :
-- Date    :
--
--------------------------------------------------------------------------------
-- Description :
--
--------------------------------------------------------------------------------

LIBRARY ieee;
USE ieee.std_logic_1164.all;
use ieee.std_logic_unsigned.all;

ENTITY rom_8x4 IS
  PORT (
  	clock: in std_logic;
  	address: in std_logic_vector(2 downto 0);
  	outp: out std_logic_vector(3 downto 0)
    );
END rom_8x4;


ARCHITECTURE TypeArchitecture OF rom_8x4 IS
type matrix is array (0 to 7) of std_logic_vector(3 downto 0);
signal memory : matrix := ("0000", "0001", "0010", "0011", "0100", "0101", "0110", "0111");
BEGIN
	process(clock)
	begin
	if rising_edge(clock) then
		outp <= memory(conv_integer(address));
	end if;
	end process;

END TypeArchitecture;
