// Logisim project mux_2to1_4bit_concurent.circ as structural Verilog
module main (
  input  [3:0] in_1,
  input  [3:0] in_2,
  input  in_3,
  output [3:0] out_4
);

  mux_2to1_4bit mux_2to1_4bit_1 (.a(in_1), .b(in_2), .sel(in_3), .\output (out_4));
endmodule

// VHDL entity mux_2to1_4bit, as the project stores it:
--------------------------------------------------------------------------------
-- Project :
-- File    :
-- Autor   :
-- Date    :
--
--------------------------------------------------------------------------------
-- Description :
--
--------------------------------------------------------------------------------

LIBRARY ieee;
USE ieee.std_logic_1164.all;

ENTITY mux_2to1_4bit IS
  PORT (
	a: in std_logic_vector(3 downto 0);
	b: in std_logic_vector(3 downto 0);
	sel: in std_logic;
	output: out std_logic_vector(3 downto 0)
    );
END mux_2to1_4bit;

--------------------------------------------------------------------------------
--Complete your VHDL description below
--------------------------------------------------------------------------------

ARCHITECTURE TypeArchitecture OF mux_2to1_4bit IS

BEGIN
	output <= a when sel = '0' else b;

END TypeArchitecture;
