// Logisim project nnumarator_4b_struct.circ as structural Verilog
module main (
  output [3:0] out_1
);

  wire clock_1_out;

  Clock clock_1 (.out(clock_1_out));
  numarator_4b_struct numarator_4b_struct_1 (.clk(clock_1_out), .o(out_1));
endmodule

// VHDL entity numarator_4b_struct, as the project stores it:
--------------------------------------------------------------------------------
-- Project :
-- File    :
-- Autor   :
-- Date    :
--
--------------------------------------------------------------------------------
-- Description :
--
--------------------------------------------------------------------------------

LIBRARY ieee;
USE ieee.std_logic_1164.all;

ENTITY numarator_4b_struct IS
  PORT (
	clk : in std_logic;
	o : out std_logic_vector(3 downto 0)
    );
END numarator_4b_struct;

--------------------------------------------------------------------------------
--Complete your VHDL description below
--------------------------------------------------------------------------------

ARCHITECTURE TypeArchitecture OF numarator_4b_struct IS
COMPONENT numarator_2b IS
  PORT (
	clk: in std_logic;
	o: out std_logic_vector(1 downto 0);
	full: out std_logic
    );
END COMPONENT;
signal sumL, sumH : std_logic_vector(1 downto 0) := "00";
signal incr, discard: std_logic := '0';
BEGIN
C1: numarator_2b port map(clk, sumL, incr);
C2: numarator_2b port map(incr, sumH, discard);

o <= sumH & sumL;
END TypeArchitecture;







LIBRARY ieee;
USE ieee.std_logic_1164.all;
use ieee.std_logic_unsigned.all;

ENTITY numarator_2b IS
  PORT (
	clk: in std_logic;
	o: out std_logic_vector(1 downto 0);
	full: out std_logic
    );
END numarator_2b;

--------------------------------------------------------------------------------
--Complete your VHDL description below
--------------------------------------------------------------------------------

ARCHITECTURE TypeArchitecture OF numarator_2b IS
signal number : std_logic_vector(1 downto 0) := "00";
BEGIN
	process(clk)
	begin
		if rising_edge(clk) then
			full <= '0';
			if number = "11" then
				full <= '1';
				number <= "00";
			else 
				number <= number + 1;
				
			end if;
		end if;
		o <= number;
	end process;

END TypeArchitecture;
