// Logisim project t_sincronn.circ as structural Verilog
module main (
  input  in_1,
  input  in_2,
  input  in_3,
  output out_4
);

  wire clock_1_out;

  Clock clock_1 (.out(clock_1_out));
  t_sincron t_sincron_1 (.clk(clock_1_out), .t(in_1), .s(in_2), .r(in_3), .\output (out_4));
endmodule

// VHDL entity t_sincron, as the project stores it:
--------------------------------------------------------------------------------
-- Project :
-- File    :
-- Autor   :
-- Date    :
--
--------------------------------------------------------------------------------
-- Description :
--
--------------------------------------------------------------------------------

LIBRARY ieee;
USE ieee.std_logic_1164.all;

ENTITY t_sincron IS
  PORT (
  	clk: in std_logic;
	t,s,r: in std_logic;
	output: out std_logic
    );
END t_sincron;

--------------------------------------------------------------------------------
--Complete your VHDL description below
--------------------------------------------------------------------------------

ARCHITECTURE TypeArchitecture OF t_sincron IS

signal q: std_logic := '0';
BEGIN
	process(clk)
	begin
		if s = '1' then 
			q <= '1';
		elsif r = '1' then
			q <= '0';
		elsif rising_edge(clk) then
			if t = '1' then
				q <= not q;
			else 
				q <= q;
			end if;
		end if;
		output <= q;
	end process;

END TypeArchitecture;
