// Logisim project sumator_flux.circ as structural Verilog
module main (
  input  Input_1,
  input  Input_2,
  input  Input_3,
  output Output_1,
  output Output_2
);

  sumator sumator_1 (.A(Input_1), .B(Input_2), .CIN(Input_3), .S(Output_1), .COUT(Output_2));
endmodule

// VHDL entity sumator, as the project stores it:
LIBRARY ieee;
USE ieee.std_logic_1164.ALL;

ENTITY sumator IS
	PORT (
		A, B, CIN : IN std_logic;
		S, COUT : OUT std_logic
	);
END sumator;

ARCHITECTURE flux OF sumator IS

BEGIN
	S <= A XOR B XOR CIN;
	COUT <= (A AND B) OR (A AND CIN) OR (B AND CIN);

END flux;
