// Logisim project sumator_structural.circ as structural Verilog
module main (
  input  Input_1,
  input  Input_2,
  input  Input_3,
  output Output_1,
  output Output_2
);

  sumator sumator_1 (.A(Input_1), .B(Input_2), .CIN(Input_3), .S(Output_1), .COUT(Output_2));
endmodule

// VHDL entity sumator, as the project stores it:
LIBRARY ieee;
USE ieee.std_logic_1164.ALL;

ENTITY sumator IS
	PORT (
		A, B, CIN : IN std_logic;
		S, COUT : OUT std_logic
	);
END sumator;

ARCHITECTURE structural OF sumator IS
	COMPONENT POARTA_SI
		PORT (
			X, Y : IN std_logic;
			Z : OUT std_logic
		);
	END COMPONENT;
 
	COMPONENT POARTA_XOR
		PORT (
			W, X, Y : IN std_logic;
			Z : OUT std_logic
		);
	END COMPONENT;
 
	COMPONENT POARTA_SAU
		PORT (
			W, X, Y : IN std_logic;
			Z : OUT std_logic
		);
	END COMPONENT;
 
	SIGNAL N1, N2, N3 : std_logic;
 
BEGIN
	C1 : POARTA_SI
	PORT MAP(A, B, N1);
	C2 : POARTA_SI
	PORT MAP(B, CIN, N2);
	C3 : POARTA_SAU
	PORT MAP(N1, N2, N3, COUT);
C4 : POARTA_SI
PORT MAP(A, CIN, N3);
C5 : POARTA_XOR
PORT MAP(A, B, CIN, S);
 
END ARCHITECTURE structural;
LIBRARY ieee;
USE ieee.std_logic_1164.ALL;
ENTITY POARTA_SI IS
	PORT (
	X, Y : IN std_logic;
	Z : OUT std_logic
	);
END ENTITY;

ARCHITECTURE flux OF POARTA_SI IS
BEGIN
	Z <= X AND Y;
END ARCHITECTURE;

LIBRARY ieee;
USE ieee.std_logic_1164.ALL;

ENTITY POARTA_SAU IS
	PORT (
	W, X, Y : IN std_logic;
	Z : OUT std_logic
	);
END ENTITY;

ARCHITECTURE flux OF POARTA_SAU IS
BEGIN
	Z <= X OR Y OR W;
END ARCHITECTURE;
LIBRARY ieee;
USE ieee.std_logic_1164.ALL;

ENTITY POARTA_XOR IS
	PORT (
	W, X, Y : IN std_logic;
	Z : OUT std_logic
	);
END ENTITY;

ARCHITECTURE flux OF POARTA_XOR IS
BEGIN
	Z <= X XOR Y XOR W;
END ARCHITECTURE;
