// Logisim project comparator_2biti.circ as structural Verilog
module main (
  input  [1:0] Input_bus_1,
  input  [1:0] Input_bus_2,
  output Output_1,
  output Output_2,
  output Output_3
);

  comparator2 comparator2_1 (.A(Input_bus_1), .B(Input_bus_2), .LESS(Output_1), .GREATER(Output_2), .EQUAL(Output_3));
endmodule

// VHDL entity comparator2, as the project stores it:
LIBRARY ieee;
USE ieee.std_logic_1164.all;

ENTITY comparator2 IS
  PORT (
	A, B : in std_logic_vector(1 DOWNTO 0);
	LESS, GREATER, EQUAL : out std_logic
    );
END comparator2;

--------------------------------------------------------------------------------
--Complete your VHDL description below
--------------------------------------------------------------------------------

ARCHITECTURE TypeArchitecture OF comparator2 IS


BEGIN
	process(A, B)
	begin
		if A(1) > B(1) then
			LESS <= '0';
			GREATER <= '1';
			EQUAL <= '0';
		elsif A(1) < B(1) then
			LESS <= '1';
			GREATER <= '0';
			EQUAL <= '0';
		else 
			if A(0) > B(0) then
				LESS <= '0';
				GREATER <= '1';
				EQUAL <= '0';
			elsif A(0) < B(0) then
				LESS <= '1';
				GREATER <= '0';
				EQUAL <= '0';
			else
				LESS <= '0';
				GREATER <= '0';
				EQUAL <= '1';
			end if;
		end if;
	end process;

END TypeArchitecture;
