// Logisim project mux_n_1.circ as structural Verilog
module main (
  input  [4:0] in_1,
  input  [2:0] in_2,
  output out_3
);

  wire [7:5] undriven;

  muxn_1 muxn_1_1 (.A({undriven, in_1}), .SEL(in_2), .Y(out_3));
  // Pins of 5 and 8 bits meet at {undriven, in_1}
endmodule

// VHDL entity muxn_1, as the project stores it:
LIBRARY ieee;
USE ieee.std_logic_1164.all;
use ieee.std_logic_unsigned.all;

ENTITY muxn_1 IS
  PORT (
	--generic (...)
	--8:1 pt. ca nu merge generic
	--logica la generic va implica ceil(log2(n)) pentru a gasi nr. de biti necesari pentru selectie 
	A : in std_logic_vector(7 downto 0);
	SEL : in std_logic_vector(3 downto 1);
	Y : out std_logic
    );
END muxn_1;

ARCHITECTURE TypeArchitecture OF muxn_1 IS

BEGIN
	Y <= A(conv_integer(SEL));

END TypeArchitecture;
