// Logisim project sumator3biti.circ as structural Verilog
module main (
  input  [2:0] Input_bus_1,
  input  [2:0] Input_bus_2,
  input  Input_1,
  output [2:0] Output_bus_1,
  output Output_1
);

  sumator3 sumator3_1 (.A(Input_bus_1), .B(Input_bus_2), .CIN(Input_1), .S(Output_bus_1), .COUT(Output_1));
endmodule

// VHDL entity sumator3, as the project stores it:
LIBRARY ieee;
USE ieee.std_logic_1164.ALL;

entity sumator3 is
	port (
		A, B: in std_logic_vector(2 downto 0);
		CIN : in std_logic;
		S: out std_logic_vector(2 downto 0);
		COUT: out std_logic
	);
end sumator3;

architecture structural of sumator3 is
	component sumator 
		PORT (
			A, B, CIN : IN std_logic;
			S, COUT : OUT std_logic
		);
	end component;
	signal CR1, CR2: std_logic;
begin
S1 : sumator port map(A(0), B(0), CIN, S(0), CR1);
S2 : sumator port map(A(1), B(1), CR1, S(1), CR2);
S3 : sumator port map(A(2), B(2), CR2, S(2), COUT);
end architecture structural;



LIBRARY ieee;
USE ieee.std_logic_1164.ALL;

ENTITY sumator IS
	PORT (
		A, B, CIN : IN std_logic;
		S, COUT : OUT std_logic
	);
END sumator;

ARCHITECTURE structural OF sumator IS
	COMPONENT POARTA_SI
		PORT (
			X, Y : IN std_logic;
			Z : OUT std_logic
		);
	END COMPONENT;
 
	COMPONENT POARTA_XOR
		PORT (
			W, X, Y : IN std_logic;
			Z : OUT std_logic
		);
	END COMPONENT;
 
	COMPONENT POARTA_SAU
		PORT (
			W, X, Y : IN std_logic;
			Z : OUT std_logic
		);
	END COMPONENT;
 
	SIGNAL N1, N2, N3 : std_logic;
 
BEGIN
	C1 : POARTA_SI
	PORT MAP(A, B, N1);
	C2 : POARTA_SI
	PORT MAP(B, CIN, N2);
	C3 : POARTA_SAU
	PORT MAP(N1, N2, N3, COUT);
C4 : POARTA_SI
PORT MAP(A, CIN, N3);
C5 : POARTA_XOR
PORT MAP(A, B, CIN, S);
 
END ARCHITECTURE structural;
LIBRARY ieee;
USE ieee.std_logic_1164.ALL;
ENTITY POARTA_SI IS
	PORT (
	X, Y : IN std_logic;
	Z : OUT std_logic
	);
END ENTITY;

ARCHITECTURE flux OF POARTA_SI IS
BEGIN
	Z <= X AND Y;
END ARCHITECTURE;

LIBRARY ieee;
USE ieee.std_logic_1164.ALL;

ENTITY POARTA_SAU IS
	PORT (
	W, X, Y : IN std_logic;
	Z : OUT std_logic
	);
END ENTITY;

ARCHITECTURE flux OF POARTA_SAU IS
BEGIN
	Z <= X OR Y OR W;
END ARCHITECTURE;
LIBRARY ieee;
USE ieee.std_logic_1164.ALL;

ENTITY POARTA_XOR IS
	PORT (
	W, X, Y : IN std_logic;
	Z : OUT std_logic
	);
END ENTITY;

ARCHITECTURE flux OF POARTA_XOR IS
BEGIN
	Z <= X XOR Y XOR W;
END ARCHITECTURE;
