// Logisim project div_clk_si_bistabil_d.circ as structural Verilog
module main (
  input  CLK_100,
  input  RST_DIV,
  input  D,
  input  S,
  input  R,
  output Q
);

  wire divizor_f_1_clk_1;

  divizor_f divizor_f_1 (.CLK_100(CLK_100), .RST(RST_DIV), .CLK_1(divizor_f_1_clk_1));
  bistabil_d bistabil_d_1 (.CLK(divizor_f_1_clk_1), .D(D), .S(S), .R(R), .Q(Q));
endmodule

// VHDL entity divizor_f, as the project stores it:
LIBRARY ieee;
USE ieee.std_logic_1164.all;
USE ieee.std_logic_unsigned.all;

ENTITY divizor_f IS
  PORT (
  	CLK_100: in std_logic;
  	RST: in std_logic;
  	CLK_1: out std_logic
	);
END divizor_f;


ARCHITECTURE comportm OF divizor_f IS

BEGIN
	process(CLK_100)
	variable nr: std_logic_vector (25 downto 0) := (others => '0');
	begin
		if rising_edge(CLK_100) then
			if RST = '0' then
				nr := (others => '0');
			else
				nr := nr + 1;
			end if;
		end if;
		CLK_1 <= nr(25);
	end process;

END comportm;

// VHDL entity bistabil_d, as the project stores it:
LIBRARY ieee;
USE ieee.std_logic_1164.all;
USE ieee.std_logic_unsigned.all;

ENTITY bistabil_d IS
  PORT (
	CLK: in std_logic;
	D, S, R: in std_logic;
	Q: out std_logic
    );
END bistabil_d;


ARCHITECTURE compr OF bistabil_d IS

BEGIN
	process(CLK)
	begin
		if rising_edge(CLK) then
			if (S = '0') then
				Q <= '1';
			elsif (R = '0') then
				Q <= '0';
			else 
				Q <= D;
			end if;
		end if;
	end process;

END compr;
