// Logisim project divizor_clk_exact - Copy.circ as structural Verilog
module main (
  input  CLK100,
  input  RST,
  output CLK1
);

  divizor_exact divizor_exact_1 (.CLK_100D(CLK100), .RSTD(RST), .CLK_1D(CLK1));
endmodule

// VHDL entity divizor_exact, as the project stores it:
LIBRARY ieee;
USE ieee.std_logic_1164.all;
USE ieee.std_logic_unsigned.all;

ENTITY divizor_exact is
	PORT (
		CLK_100D, RSTD : in std_logic;
		CLK_1D : out std_logic
	);
end divizor_exact;

ARCHITECTURE structr of divizor_exact is
	COMPONENT NUM_MOD IS
	  PORT (
		CLK_100 : in std_logic;
		RST: in std_logic;
	  	TOG: out std_logic
	    );
	END COMPONENT;
	
	COMPONENT BISTABIL_T is 
		PORT (
			CLK, T : in std_logic;
			Q : out std_logic
		);
	END COMPONENT;
	
	signal W1: std_logic;

begin
	D1 : NUM_MOD port map(CLK_100D, RSTD, W1);
	T1 : BISTABIL_T port map(CLK_100D, W1, CLK_1D);
end structr;




-- Numarator




LIBRARY ieee;
USE ieee.std_logic_1164.all;
USE ieee.std_logic_unsigned.all;

ENTITY NUM_MOD IS
  PORT (
	CLK_100 : in std_logic;
	RST: in std_logic;
  	TOG: out std_logic
    );
END NUM_MOD;


ARCHITECTURE Comportamental OF NUM_MOD IS

BEGIN
	process(CLK_100)
	variable count: std_logic_vector (25 downto 0) := (others => '0');
	constant modl: std_logic_vector (25 downto 0) := "10111110101111000010000000";--"10111110101111000010000000";
	begin
		if rising_edge(CLK_100) then
			if RST = '0' then
				count := (others => '0');
			else 
				count := count + 1;
			end if;
			
			if count = modl then
				count := (others => '0');
				TOG <= '1';
			else
				TOG <= '0';
			end if;
				
		end if;
		
	end process;

END Comportamental;




-- Bistabil T



LIBRARY ieee;
USE ieee.std_logic_1164.all;
USE ieee.std_logic_unsigned.all;

ENTITY BISTABIL_T is 
	PORT (
		CLK, T : in std_logic;
		Q : out std_logic
	);
END BISTABIL_T;

ARCHITECTURE Comportamental of BISTABIL_T is
	signal tmp : std_logic := '0';
BEGIN
	process(CLK)
	begin
		if rising_edge(CLK) then
			if T = '1' then
				tmp <= not tmp;
			else 
				tmp <= tmp;
			end if;
			Q <= tmp;
		end if;
	end process;
END Comportamental;
