// Logisim project numarator_lp_4bits.circ as structural Verilog
module main (
  input  Input_1,
  input  Input_2,
  input  Input_3,
  input  Input_4,
  input  [3:0] Input_bus_1,
  output [3:0] Output_bus_1
);

  wire divizor_f_1_clk_1;

  divizor_f divizor_f_1 (.CLK_100(Input_1), .RST(Input_2), .CLK_1(divizor_f_1_clk_1));
  numarator_indirect_4b numarator_indirect_4b_1 (
    .CLK(divizor_f_1_clk_1), .LP(Input_3), .RST(Input_4), .LD(Input_bus_1), .Q(Output_bus_1));
endmodule

// VHDL entity numarator_indirect_4b, as the project stores it:
LIBRARY ieee;
USE ieee.std_logic_1164.all;
use ieee.std_logic_unsigned.all;

--Indirect = ??

ENTITY numarator_indirect_4b IS
  PORT (
  	CLK, LP, RST : in std_logic;
  	LD : in std_logic_vector(3 downto 0);
  	Q : out std_logic_vector(3 downto 0)
  	
    );
END numarator_indirect_4b;


ARCHITECTURE TypeArchitecture OF numarator_indirect_4b IS

BEGIN
	process(CLK)
	variable tmp : std_logic_vector(3 downto 0) := "0000";
	begin
		if rising_edge(CLK) then
			if (RST = '0') then
				tmp := "0000";
			elsif (LP = '0') then
				tmp := LD;
			else
				tmp := tmp + 1;				
			end if;
		end if;
		Q <= tmp;
	end process;

END TypeArchitecture;

// VHDL entity divizor_f, as the project stores it:
LIBRARY ieee;
USE ieee.std_logic_1164.all;
USE ieee.std_logic_unsigned.all;

ENTITY divizor_f IS
  PORT (
  	CLK_100: in std_logic;
  	RST: in std_logic;
  	CLK_1: out std_logic
	);
END divizor_f;


ARCHITECTURE comportm OF divizor_f IS

BEGIN

	process(CLK_100)
	variable nr: std_logic_vector (25 downto 0) := (others => '0');
	begin
		if rising_edge(CLK_100) then
			if RST = '0' then
				nr := (others => '0');
			else
				nr := nr + 1;
			end if;
		end if;
		CLK_1 <= nr(25);
	end process;

END comportm;
