// Logisim project shift_register_4bits.circ as structural Verilog
module main (
  input  CLOCK,
  input  RESET,
  input  INPT,
  output [3:0] OUTP
);

  shift_register4b shift_register4b_1 (.CLK(CLOCK), .RST(RESET), .INPT(INPT), .OUTP(OUTP));
endmodule

// VHDL entity shift_register4b, as the project stores it:
LIBRARY ieee;
USE ieee.std_logic_1164.all;
USE ieee.std_logic_unsigned.all;

ENTITY shift_register4b IS
  PORT (
	CLK, RST, INPT : in std_logic;
	OUTP : out std_logic_vector(3 downto 0)
    );
END shift_register4b;

--------------------------------------------------------------------------------
--Complete your VHDL description below
--------------------------------------------------------------------------------

ARCHITECTURE structr OF shift_register4b IS
	component bistabil_d IS
	  PORT (
		CLK: in std_logic;
		D, S, R: in std_logic;
		Q: out std_logic
	    );
	END component;
	
	component divizor_f IS
	  PORT (
	  	CLK_100: in std_logic;
	  	RST: in std_logic;
	  	CLK_1: out std_logic
		);
	END component;
	signal W1, W2, W3 , CLK1: std_logic;
BEGIN
	DC : divizor_f port map (CLK, RST, CLK1);
	D0: bistabil_d port map (CLK1, INPT, '1', RST, W1);
	OUTP(3) <= W1;
	D1 : bistabil_d port map (CLK1, W1, '1', RST, W2);
	OUTP(2) <= W2;
	D2 : bistabil_d port map (CLK1, W2, '1', RST, W3);
	OUTP(1) <= W3;
	D3 : bistabil_d port map (CLK1, W3, '1', RST, OUTP(0));

END structr;



LIBRARY ieee;
USE ieee.std_logic_1164.all;
USE ieee.std_logic_unsigned.all;

ENTITY bistabil_d IS
  PORT (
	CLK: in std_logic;
	D, S, R: in std_logic;
	Q: out std_logic
    );
END bistabil_d;


ARCHITECTURE compr OF bistabil_d IS

BEGIN

	process(CLK)
	begin
		if rising_edge(CLK) then
			if (S = '0') then
				Q <= '1';
			elsif (R = '0') then
				Q <= '0';
			else 
				Q <= D;
			end if;
		end if;
	end process;

END compr;

LIBRARY ieee;
USE ieee.std_logic_1164.all;
USE ieee.std_logic_unsigned.all;

ENTITY divizor_f IS
  PORT (
  	CLK_100: in std_logic;
  	RST: in std_logic;
  	CLK_1: out std_logic
	);
END divizor_f;


ARCHITECTURE comportm OF divizor_f IS

BEGIN

	process(CLK_100)
	variable nr: std_logic_vector (25 downto 0) := (others => '0');
	begin
		if rising_edge(CLK_100) then
			if RST = '0' then
				nr := (others => '0');
			else
				nr := nr + 1;
			end if;
		end if;
		CLK_1 <= nr(25);
	end process;

END comportm;
