// Logisim project univ_shift_register_4bits.circ as structural Verilog
module main (
  input  Input_1,
  input  Input_2,
  input  Input_3,
  input  [1:0] Input_bus_1,
  input  [3:0] Input_bus_2,
  input  in_6,
  output [3:0] Output_bus_1
);

  wire divizor_f_1_clk_1;

  divizor_f divizor_f_1 (.CLK_100(Input_1), .RST(Input_2), .CLK_1(divizor_f_1_clk_1));
  universal_shift_register_4b universal_shift_register_4b_1 (
    .CLK(divizor_f_1_clk_1), .INPT(Input_3), .S(Input_bus_1), .LD(Input_bus_2), .CLR(in_6), .Q(Output_bus_1));
endmodule

// VHDL entity universal_shift_register_4b, as the project stores it:
LIBRARY ieee;
USE ieee.std_logic_1164.all;
USE ieee.std_logic_unsigned.all;

ENTITY universal_shift_register_4b IS
  PORT (
	CLK, INPT : in std_logic;
	S: in std_logic_vector(1 downto 0);
	LD : in std_logic_vector(3 downto 0);
	CLR : in std_logic;
	Q : out std_logic_vector(3 downto 0)
    );
END universal_shift_register_4b;

ARCHITECTURE comportm OF universal_shift_register_4b IS

BEGIN
	process(CLK)
	variable tmp : std_logic_vector(3 downto 0) := "0000";
	begin
		if rising_edge(CLK) then
			if (CLR = '0') then 
				tmp := "0000";
			else
				if (S = "01") then
					tmp(0) := tmp(1);
					tmp(1) := tmp(2);
					tmp(2) := tmp(3);
					tmp(3) := INPT;
				elsif (S = "10") then
					tmp(3) := tmp(2);
					tmp(2) := tmp(1);
					tmp(1) := tmp(0);
					tmp(0) := INPT;
				elsif (S = "11") then
					tmp := LD;
				else
					
				end if;
			end if;
			Q <= tmp;
		end if;
	end process;


END comportm;

// VHDL entity divizor_f, as the project stores it:
LIBRARY ieee;
USE ieee.std_logic_1164.all;
USE ieee.std_logic_unsigned.all;

ENTITY divizor_f IS
  PORT (
  	CLK_100: in std_logic;
  	RST: in std_logic;
  	CLK_1: out std_logic
	);
END divizor_f;


ARCHITECTURE comportm OF divizor_f IS

BEGIN

	process(CLK_100)
	variable nr: std_logic_vector (25 downto 0) := (others => '0');
	begin
		if rising_edge(CLK_100) then
			if RST = '0' then
				nr := (others => '0');
			else
				nr := nr + 1;
			end if;
		end if;
		CLK_1 <= nr(25);
	end process;

END comportm;
