// Logisim project adder8bit.circ as structural Verilog
module main (
  input  [7:0] INPT,
  input  B_OK,
  input  B_START,
  input  B_RESET,
  output Output_1,
  output Output_2,
  output Output_3,
  output Output_4,
  output [3:0] ANODE_OUT,
  output [6:0] SSD_OUT
);

  wire adder8nr_1_load, adder8nr_1_reset, clock_1_out, debouncer_1_btn_db, debouncer_2_btn_db,
       debouncer_3_btn_db, divizor_f_1_clk_1, ssd_controller_1_reset_decd;
  wire [1:0] ssd_controller_1_anode;
  wire [7:0] adder_1_out, register_1_q;

  Clock clock_1 (.out(clock_1_out));
  debouncer debouncer_1 (.CLK(clock_1_out), .BTN(B_OK), .BTN_DB(debouncer_1_btn_db));
  debouncer debouncer_2 (.CLK(clock_1_out), .BTN(B_START), .BTN_DB(debouncer_2_btn_db));
  debouncer debouncer_3 (.CLK(clock_1_out), .BTN(B_RESET), .BTN_DB(debouncer_3_btn_db));
  divizor_f divizor_f_1 (.CLK_100(clock_1_out), .RST(1'b1), .CLK_1(divizor_f_1_clk_1));
  adder8nr adder8nr_1 (
    .CLK(clock_1_out), .OK(debouncer_1_btn_db), .START(debouncer_2_btn_db), .RESETIN(debouncer_3_btn_db),
    .WAITING(Output_1), .LAST(Output_2), .FINISH(Output_3), .INSERT(Output_4), .LOAD(adder8nr_1_load),
    .RESET(adder8nr_1_reset));
  ssd_controller ssd_controller_1 (
    .REDUCED_CLK(divizor_f_1_clk_1), .RESET(debouncer_3_btn_db), .ANODE(ssd_controller_1_anode),
    .RESET_DECD(ssd_controller_1_reset_decd));
  Register register_1 (
    .D(adder_1_out), .en(adder8nr_1_load), .clk(clock_1_out), .Q(register_1_q), .clr(adder8nr_1_reset));
  Adder adder_1 (.a(INPT), .b(register_1_q), .out(adder_1_out));  // open: cin, cout
  ssd_decd ssd_decd_1 (
    .CLK(clock_1_out), .RESET(ssd_controller_1_reset_decd), .ANODE_IN(ssd_controller_1_anode),
    .NR({{8{1'b0}}, register_1_q}), .ANODE_OUT(ANODE_OUT), .SSD_OUT(SSD_OUT));
endmodule

// VHDL entity adder8nr, as the project stores it:
LIBRARY ieee;
USE ieee.std_logic_1164.all;

ENTITY adder8nr IS
  PORT (
  	CLK, OK, START, RESETIN: in std_logic;
  	WAITING, LAST, FINISH, INSERT, LOAD, RESET: out std_logic
    );
END adder8nr;


ARCHITECTURE comportm OF adder8nr IS
type STARE_T is (IDLE0, N1, N2, N3, N4, N5, N6, N7, N8, IDLE1);
signal STARE, NXSTARE : STARE_T;
signal PREV_OK, PREV_START: std_logic;
BEGIN

UPDATE_STARE: process (RESETIN, CLK)
begin
	if (RESETIN = '1') then
		STARE <= IDLE0;
	elsif rising_edge(CLK) then
		STARE <= NXSTARE;
	end if;
end process UPDATE_STARE;

TRANZITII: process(STARE, OK, START)
begin
	WAITING <= '0'; LAST <= '0'; FINISH<= '0'; INSERT <= '0'; LOAD <= '0'; RESET <= '0';
	case stare is
		when IDLE0 => WAITING <= '1';
			if (START = '0') then
				NXSTARE <= IDLE0;
			else
			   NXSTARE <= N1;
			   RESET <= '1';
			end if;
		when N1 => 
			if (OK = '1' and PREV_OK = '0') then
				LOAD <= '1';
				NXSTARE <= N2;
			else 
				INSERT <= '1'; 
				NXSTARE <= N1;
				
			end if;
		when N2 => 
			if (OK = '1' and PREV_OK = '0') then
				LOAD <= '1';
				NXSTARE <= N3;
			else 
				INSERT <= '1';
				NXSTARE <= N2;
			end if;
		when N3 =>
			if (OK = '1' and PREV_OK = '0') then
				LOAD <= '1';
				NXSTARE <= N4;
			else 
				INSERT <= '1';
				NXSTARE <= N3;
			end if;
		when N4 => 
			if (OK = '1' and PREV_OK = '0') then
				LOAD <= '1';
				NXSTARE <= N5;
			else 
				INSERT <= '1';
				NXSTARE <= N4;
			end if;
		when N5 => 
			if (OK = '1' and PREV_OK = '0') then
				LOAD <= '1';
				NXSTARE <= N6;
			else 
				INSERT <= '1';
				NXSTARE <= N5;
			end if;
		when N6 => 
			if (OK = '1' and PREV_OK = '0') then

				LOAD <= '1';
				NXSTARE <= N7;
			else 			
				INSERT <= '1';
				NXSTARE <= N6;
				
			end if;
		when N7 =>
			if (OK = '1' and PREV_OK = '0') then 
				LOAD <= '1';
				NXSTARE <= N8;
			else 
				INSERT <= '1';
				NXSTARE <= N7;
			end if;
		when N8 => 
			if (OK = '1' and PREV_OK = '0') then
				LOAD <= '1';
				NXSTARE <= IDLE1;
			else 
				INSERT <= '1';
				LAST <= '1';
				NXSTARE <= N8;
			end if;
		when IDLE1 => FINISH <= '1';
			if (START = '1' and PREV_START = '0') then
				RESET <= '1';
				NXSTARE <= N1;
			else
				FINISH <= '1';
				NXSTARE <= IDLE1;
			end if;

	end case;
	if OK = '1' then PREV_OK <= '1'; else PREV_OK <= '0'; end if;
	if START = '1' then PREV_START <= '1'; else PREV_START <= '0'; end if;
			
end process TRANZITII;


END comportm;

// VHDL entity debouncer, as the project stores it:
LIBRARY ieee;
USE ieee.std_logic_1164.all;
USE ieee.std_logic_unsigned.all;

ENTITY debouncer IS
  PORT (
	CLK, BTN: in std_logic;
	BTN_DB: out std_logic
    );
END debouncer;


ARCHITECTURE structr OF debouncer IS
	component bistabil_d is
	  PORT (
		CLK: in std_logic;
		D, S, R: in std_logic;
		Q: out std_logic
	    );
	END component;

	component POARTA_SI is
		PORT (
		X, Y, Z, A, B: IN std_logic;
		W : OUT std_logic
		);
	END component;

	signal Q2, Q1, Q0, W5, W4: std_logic;

BEGIN
	AP : POARTA_SI port map (Q2, Q1, Q0, W5, W4, BTN_DB);
	D1 : bistabil_d port map(CLK, BTN, '1', '1', Q2);
	D2 : bistabil_d port map(CLK, Q2, '1', '1', Q1);
	D3 : bistabil_d port map(CLK, Q1, '1', '1', Q0);
	D4 : bistabil_d port map(CLK, Q0, '1', '1', W5);
	D5 : bistabil_d port map(CLK, W5, '1', '1', W4);
	

END structr;




LIBRARY ieee;
USE ieee.std_logic_1164.all;
USE ieee.std_logic_unsigned.all;

ENTITY bistabil_d IS
  PORT (
	CLK: in std_logic;
	D, S, R: in std_logic;
	Q: out std_logic
    );
END bistabil_d;


ARCHITECTURE compr OF bistabil_d IS

BEGIN

	process(CLK)
	begin
		if rising_edge(CLK) then
			if (S = '0') then
				Q <= '1';
			elsif (R = '0') then
				Q <= '0';
			else 
				Q <= D;
			end if;
		end if;
	end process;

END compr;




LIBRARY ieee;
USE ieee.std_logic_1164.all;
USE ieee.std_logic_unsigned.all;

ENTITY divizor_f IS
  PORT (
  	CLK_100: in std_logic;
  	RST: in std_logic;
  	CLK_1: out std_logic
	);
END divizor_f;


ARCHITECTURE comportm OF divizor_f IS

BEGIN

	process(CLK_100)
	variable nr: std_logic_vector (25 downto 0) := (others => '0');
	begin
		if rising_edge(CLK_100) then
			if RST = '0' then
				nr := (others => '0');
			else
				nr := nr + 1;
			end if; 
		end if;
		CLK_1 <= nr(25);
	end process;

END comportm;

LIBRARY ieee;
USE ieee.std_logic_1164.ALL;
ENTITY POARTA_SI IS
	PORT (
	X, Y, Z, A, B: IN std_logic;
	W : OUT std_logic
	);
END ENTITY;

ARCHITECTURE flux OF POARTA_SI IS
BEGIN
	W <= X AND Y AND Z AND A AND B;
END ARCHITECTURE;

// VHDL entity ssd_controller, as the project stores it:
--------------------------------------------------------------------------------
-- Project :
-- File    :
-- Autor   :
-- Date    :
--
--------------------------------------------------------------------------------
-- Description :
--
--------------------------------------------------------------------------------

LIBRARY ieee;
USE ieee.std_logic_1164.all;
USE ieee.std_logic_unsigned.all;

ENTITY ssd_controller IS
  PORT (
	REDUCED_CLK, RESET: in std_logic;
	ANODE: out std_logic_vector(1 downto 0);
	RESET_DECD: out std_logic
    );
END ssd_controller;

--------------------------------------------------------------------------------
--Complete your VHDL description below
--------------------------------------------------------------------------------

ARCHITECTURE comprtm OF ssd_controller IS
type STARE_T is (D0, D1, D2, D3);
signal STARE, NXSTARE : STARE_T;
BEGIN

	CTRL: process(REDUCED_CLK, RESET)
	begin
		if RESET = '1' then
			RESET_DECD <= '1';
			STARE <= D0;
		elsif rising_edge(REDUCED_CLK) then
			STARE <= NXSTARE;
			RESET_DECD <= '0';
		end if;
		
	end process CTRL;

	TRANZ: process(STARE)
	
	begin
		ANODE <= "00";
		case STARE is
			when D0 => ANODE <= "00"; NXSTARE <= D1;
			when D1 => ANODE <= "01"; NXSTARE <= D2;
			when D2 => ANODE <= "10"; NXSTARE <= D3;
			when D3 => ANODE <= "11"; NXSTARE <= D0;
		end case;
	end process TRANZ;
	

END comprtm;

// VHDL entity ssd_decd, as the project stores it:
--------------------------------------------------------------------------------
-- Project :
-- File    :
-- Autor   :
-- Date    :
--
--------------------------------------------------------------------------------
-- Description :
--
--------------------------------------------------------------------------------

LIBRARY ieee;
USE ieee.std_logic_1164.all;
use ieee.std_logic_unsigned.all;
use ieee.numeric_std.all;

ENTITY ssd_decd IS
  PORT (
  	CLK, RESET: in std_logic;
	ANODE_IN :in std_logic_vector(1 downto 0);
	NR: in std_logic_vector(15 downto 0);
	ANODE_OUT : out std_logic_vector(3 downto 0);
	SSD_OUT: out std_logic_vector(6 downto 0)
    );
END ssd_decd;

--------------------------------------------------------------------------------
--Complete your VHDL description below
--------------------------------------------------------------------------------

ARCHITECTURE comportm OF ssd_decd IS

signal BIN_NR : std_logic_vector(3 downto 0);
BEGIN

	process(CLK, RESET)
	variable temp: integer;
	begin
--		BIN_NR <= "0000";
--		ANODE_OUT <= "0000";
		if RESET = '1' then		
			ANODE_OUT <= "0000";
			SSD_OUT <= "0000000";
		elsif rising_edge(CLK) then
			--Afisarea se face in hexa dar se poate modifica in zecimal daca trec la integer si tot iau ultima cifra
--			case ANODE_IN is
--				when "00" => BIN_NR <= NR(3 downto 0); ANODE_OUT <= "0001";
--				when "01" => BIN_NR <= NR(7 downto 4); ANODE_OUT <= "0010";
--				when "10" => BIN_NR <= NR(11 downto 8); ANODE_OUT <= "0100";
--				when "11" => BIN_NR <= NR(15 downto 12); ANODE_OUT <= "1000";
--				when others => ANODE_OUT <= "0000";
--			end case;
			temp := conv_integer(NR);
			case ANODE_IN is
				when "00" => BIN_NR <= std_logic_vector(to_unsigned(temp rem 10, BIN_NR'length)); ANODE_OUT <= "0001";
				when "01" => BIN_NR <= std_logic_vector(to_unsigned((temp / 10 ) rem 10, BIN_NR'length)); ANODE_OUT <= "0010";
				when "10" => BIN_NR <= std_logic_vector(to_unsigned((temp / 100) rem 10, BIN_NR'length)); ANODE_OUT <= "0100";
				when "11" => BIN_NR <= std_logic_vector(to_unsigned((temp / 1000) rem 10, BIN_NR'length)); ANODE_OUT <= "1000";
				when others => ANODE_OUT <= "0000";
			end case;
			
			SSD_OUT <= "0000000";
			case BIN_NR is
				when "0000" => SSD_OUT <= "1111110";
				when "0001" => SSD_OUT <= "0110000";
				when "0010" => SSD_OUT <= "1101101";
				when "0011" => SSD_OUT <= "1111001";
				when "0100" => SSD_OUT <= "0110011";
				when "0101" => SSD_OUT <= "1011011";
				when "0110" => SSD_OUT <= "0011111";
				when "0111" => SSD_OUT <= "1110000";
				when "1000" => SSD_OUT <= "1111111";
				when "1001" => SSD_OUT <= "1110011";
				when "1010" => SSD_OUT <= "1110111";
				when "1011" => SSD_OUT <= "0011111";
				when "1100" => SSD_OUT <= "1001110";
				when "1101" => SSD_OUT <= "0111101";
				when "1110" => SSD_OUT <= "1001111";
				when "1111" => SSD_OUT <= "1000111";
				when others => SSD_OUT <= "0000000";
			end case;
		end if;
	end process;

END comportm;

// VHDL entity divizor_f, as the project stores it:
LIBRARY ieee;
USE ieee.std_logic_1164.all;
USE ieee.std_logic_unsigned.all;

ENTITY divizor_f IS
  PORT (
  	CLK_100: in std_logic;
  	RST: in std_logic;
  	CLK_1: out std_logic
	);
END divizor_f;


ARCHITECTURE comportm OF divizor_f IS

BEGIN

	process(CLK_100)
	variable nr: std_logic_vector (10 downto 0) := (others => '0');
	begin
		if rising_edge(CLK_100) then
			if RST = '0' then
				nr := (others => '0');
			else
				nr := nr + 1;
			end if;
		end if;
		CLK_1 <= nr(10);
	end process;

END comportm;
