// Logisim project bcdTo_7seg.circ as structural Verilog
module main (
  input  [3:0] Input_bus_1,
  output [6:0] Output_bus_1
);

  bcdto7seg bcdto7seg_1 (.inpt(Input_bus_1), .outp(Output_bus_1));
endmodule

// VHDL entity bcdto7seg, as the project stores it:
LIBRARY ieee;
USE ieee.std_logic_1164.all;

ENTITY bcdto7seg IS
  PORT (
  	inpt: in std_logic_vector(3 downto 0);
  	outp: out std_logic_vector(6 downto 0)
    );
END bcdto7seg;

--------------------------------------------------------------------------------
--Complete your VHDL description below
--------------------------------------------------------------------------------

ARCHITECTURE TypeArchitecture OF bcdto7seg IS

BEGIN
	with inpt select outp <=
		not "1111110" when "0000",
		not "0110000" when "0001",
		not "1101101" when "0010",
		not "1111001" when "0011",
		not "0110011" when "0100",
		not "1011011" when "0101",
		not "1011111" when "0110",
		not "1110000" when "0111",
		not "1111111" when "1000",
		not "1111011" when "1001",
		not "1110111" when "1010",
		not "0011111" when "1011",
		not "1001110" when "1100",
		not "0111101" when "1101",
		not "1001111" when "1110",
		not "1000111" when "1111",
		not "0000000" when others;
		

END TypeArchitecture;
