// Logisim project exerc.circ as structural Verilog
module main (
  input  [7:0] Mi,
  input  [2:0] Ms,
  input  Di,
  input  [2:0] Ds,
  input  [3:0] An1,
  input  [3:0] An2,
  input  [2:0] Aop,
  output Mo,
  output [7:0] Do,
  output [3:0] Arez,
  output Azero
);

  mux mux_1 (.inpt(Mi), .sel(Ms), .outp(Mo));
  dmux dmux_1 (.inpt(Di), .sel(Ds), .outp(Do));
  alu alu_1 (.N1(An1), .N2(An2), .OP(Aop), .REZ(Arez), .ZERO(Azero));
endmodule

// VHDL entity mux, as the project stores it:
LIBRARY ieee;
USE ieee.std_logic_1164.all;

ENTITY mux IS
  PORT (
	inpt: in std_logic_vector(7 downto 0);
	sel: in std_logic_vector(2 downto 0);
	outp: out std_logic
    );
END mux;

ARCHITECTURE TypeArchitecture OF mux IS

BEGIN
--	with sel select outp <=
--		inpt(0) when "000";
	outp <= inpt(0) when sel = "000" else
		inpt(1) when sel = "001" else
	 	inpt(2) when sel = "010" else 
	 	inpt(3) when sel = "011" else
	 	inpt(4) when sel = "100" else
	 	inpt(5) when sel = "101" else
	 	inpt(6) when sel = "110" else
	 	inpt(7) when sel = "111";

END TypeArchitecture;

// VHDL entity dmux, as the project stores it:
LIBRARY ieee;
USE ieee.std_logic_1164.all;

ENTITY dmux IS
  PORT (
  	inpt: in std_logic;
	sel: in std_logic_vector(2 downto 0);
  	outp: out std_logic_vector(7 downto 0)
    );
END dmux;

--------------------------------------------------------------------------------
--Complete your VHDL description below
--------------------------------------------------------------------------------

ARCHITECTURE TypeArchitecture OF dmux IS

BEGIN
	outp(0) <= inpt and not(sel(2)) and not(sel(1)) and not(sel(0));
	outp(1) <= inpt and not(sel(2)) and not(sel(1)) and (sel(0));
	outp(2) <= inpt and not(sel(2)) and (sel(1)) and not(sel(0));
	outp(3) <= inpt and not(sel(2)) and (sel(1)) and (sel(0));
	outp(4) <= inpt and (sel(2)) and not(sel(1)) and not(sel(0));
	outp(5) <= inpt and (sel(2)) and not(sel(1)) and (sel(0));
	outp(6) <= inpt and (sel(2)) and (sel(1)) and not(sel(0));
	outp(7) <= inpt and (sel(2)) and (sel(1)) and (sel(0));

END TypeArchitecture;

// VHDL entity alu, as the project stores it:
LIBRARY ieee;
USE ieee.std_logic_1164.all;
use ieee.std_logic_unsigned.all;

ENTITY alu IS
  PORT (
	N1: in std_logic_vector(3 downto 0);
	N2: in std_logic_vector(3 downto 0);
	OP: in std_logic_vector(2 downto 0);
	REZ: out std_logic_vector(3 downto 0);
	ZERO: out std_logic
    );
END alu;

--------------------------------------------------------------------------------
--Complete your VHDL description below
--------------------------------------------------------------------------------
--Add 0, Dif 1, sra 2, sla 3, sr 4, and 5, or 6, xor 7
ARCHITECTURE TypeArchitecture OF alu IS
signal STORE: std_logic_vector(4 downto 0);
BEGIN
	with OP select STORE <=
		('0' & N1) + ('0' & N2) when "000",
		('0' & N1) - ('0' & N2) when "001",
		'0' & '0' & N1(3 downto 1) when "010",
		'0' & N1(3 downto 1) & '0' when "011",
		'0' & N1(0) & N1(3 downto 1) when "100",
		('0' & N1) and ('0' & N2) when "101",
		('0' & N1) or ('0' & N2) when "110",
		('0' & N1) xor ('0' & N2) when "111",
		"00000" when others;
		
	REZ <= STORE(3 downto 0);
	ZERO <= STORE(4);

END TypeArchitecture;
