// Logisim project priority_encoder.circ as structural Verilog
module main (
  input  [7:0] Input_bus_1,
  output [2:0] Output_bus_1
);

  priorityC priorityc_1 (.inpt(Input_bus_1), .outp(Output_bus_1));
endmodule

// VHDL entity priorityC, as the project stores it:
--------------------------------------------------------------------------------
-- Project :
-- File    :
-- Autor   :
-- Date    :
--
--------------------------------------------------------------------------------
-- Description :
--
--------------------------------------------------------------------------------

LIBRARY ieee;
USE ieee.std_logic_1164.all;

ENTITY priorityC IS
  PORT (
	inpt: in std_logic_vector(7 downto 0);
	outp: out std_logic_vector(2 downto 0)
    );
END priorityC;

--------------------------------------------------------------------------------
--Complete your VHDL description below
--------------------------------------------------------------------------------

ARCHITECTURE TypeArchitecture OF priorityC IS

BEGIN
	outp <= "000" when inpt(7) = '0' else
			"001" when inpt(7 downto 6) = "10" else
			"010" when inpt(7 downto 5) = "110" else
			"011" when inpt(7 downto 4) = "1110" else
			"100" when inpt(7 downto 3) = "11110" else
			"101" when inpt(7 downto 2) = "111110" else
			"110" when inpt(7 downto 1) = "1111110" else
			"111" when inpt(7 downto 0) = "11111110";

END TypeArchitecture;
