// Logisim project dmux4bw.circ as structural Verilog
module main (
  input  in_1,
  input  in_2,
  input  [2:0] in_3,
  input  in_4,
  input  in_5,
  input  [3:0] in_6,
  input  [2:0] in_7,
  output [7:0] out_8,
  output [7:0] out_9,
  output [7:0] out_10,
  output [7:0] out_11,
  output [3:0] out_12,
  output [3:0] out_13,
  output [3:0] out_14,
  output [3:0] out_15,
  output [3:0] out_16,
  output [3:0] out_17,
  output [3:0] out_18,
  output [3:0] out_19
);

  dmux dmux_1 (.inpt(in_1), .sel(in_3), .outp(out_8));
  dmux dmux_2 (.inpt(in_2), .sel(in_3), .outp(out_9));
  dmux dmux_3 (.inpt(in_4), .sel(in_3), .outp(out_10));
  dmux dmux_4 (.inpt(in_5), .sel(in_3), .outp(out_11));
  dmux4 dmux4_1 (
    .inp(in_6), .sel(in_7), .out0(out_12), .out1(out_13), .out2(out_14), .out3(out_15), .out4(out_16),
    .out5(out_17), .out6(out_18), .out7(out_19));
endmodule

// VHDL entity dmux4, as the project stores it:
--------------------------------------------------------------------------------
-- Project :
-- File    :
-- Autor   :
-- Date    :
--
--------------------------------------------------------------------------------
-- Description :
--
--------------------------------------------------------------------------------

LIBRARY ieee;
USE ieee.std_logic_1164.all;

ENTITY dmux4 IS
  PORT (
  	inp: in std_logic_vector(3 downto 0);
  	sel: in std_logic_vector(2 downto 0);
  	out0: out std_logic_vector(3 downto 0);
  	out1: out std_logic_vector(3 downto 0);
  	out2: out std_logic_vector(3 downto 0);
  	out3: out std_logic_vector(3 downto 0);
  	out4: out std_logic_vector(3 downto 0);
  	out5: out std_logic_vector(3 downto 0);
  	out6: out std_logic_vector(3 downto 0);
  	out7: out std_logic_vector(3 downto 0)
    );
END dmux4;

--------------------------------------------------------------------------------
--Complete your VHDL description below
--------------------------------------------------------------------------------

ARCHITECTURE Structural OF dmux4 IS
	component dmux IS
	  PORT (
	  	inpt: in std_logic;
		sel: in std_logic_vector(2 downto 0);
	  	outp: out std_logic_vector(7 downto 0)
	    );
	END component;
	signal stream1: std_logic_vector(7 downto 0);
	signal stream2: std_logic_vector(7 downto 0);
	signal stream3: std_logic_vector(7 downto 0);
	signal stream4: std_logic_vector(7 downto 0);
	
	signal streama: std_logic_vector(3 downto 0);
	signal streamb: std_logic_vector(3 downto 0);
	signal streamc: std_logic_vector(3 downto 0);
	signal streamd: std_logic_vector(3 downto 0);
	signal streame: std_logic_vector(3 downto 0);
	signal streamf: std_logic_vector(3 downto 0);
	signal streamg: std_logic_vector(3 downto 0);
	signal streamh: std_logic_vector(3 downto 0);
BEGIN
D1: dmux port map (inp(3), sel, stream1);

D2: dmux port map (inp(2), sel, stream2);

D3: dmux port map (inp(1), sel, stream3);

D4: dmux port map (inp(0), sel, stream4);

streama <= stream4(7) & stream3(7) & stream2(7) & stream1(7);
streamb <= stream4(6) & stream3(6) & stream2(6) & stream1(6);
streamc <= stream4(5) & stream3(5) & stream2(5) & stream1(5);
streamd <= stream4(4) & stream3(4) & stream2(4) & stream1(4);
streame <= stream4(3) & stream3(3) & stream2(3) & stream1(3);
streamf <= stream4(2) & stream3(2) & stream2(2) & stream1(2);
streamg <= stream4(1) & stream3(1) & stream2(1) & stream1(1);
streamh <= stream4(0) & stream3(0) & stream2(0) & stream1(0);

--Fiecare output s-ar seta cu cate o ecuatie dar nu stiu cum sa fac pe 4 biti, ce am incercat nu a functionat :(
out0 <= streama and not(sel(2)) and not(sel(1)) and not(sel(0));
out1 <= streamb and not(sel(2)) and not(sel(1)) and (sel(0));
out2 <= streamc and not(sel(2)) and (sel(1)) and not(sel(0));
out3 <= streamd and not(sel(2)) and (sel(1)) and (sel(0));
out4 <= streame and (sel(2)) and not(sel(1)) and not(sel(0));
out5 <= streamf and (sel(2)) and not(sel(1)) and (sel(0));
out6 <= streamg and (sel(2)) and (sel(1)) and not(sel(0));
out7 <= streamh and (sel(2)) and (sel(1)) and (sel(0));

END Structural;





LIBRARY ieee;
USE ieee.std_logic_1164.all;

ENTITY dmux IS
  PORT (
  	inpt: in std_logic;
	sel: in std_logic_vector(2 downto 0);
  	outp: out std_logic_vector(7 downto 0)
    );
END dmux;

--------------------------------------------------------------------------------
--Complete your VHDL description below
--------------------------------------------------------------------------------

ARCHITECTURE TypeArchitecture OF dmux IS

BEGIN

	outp(0) <= inpt and not(sel(2)) and not(sel(1)) and not(sel(0));
	outp(1) <= inpt and not(sel(2)) and not(sel(1)) and (sel(0));
	outp(2) <= inpt and not(sel(2)) and (sel(1)) and not(sel(0));
	outp(3) <= inpt and not(sel(2)) and (sel(1)) and (sel(0));
	outp(4) <= inpt and (sel(2)) and not(sel(1)) and not(sel(0));
	outp(5) <= inpt and (sel(2)) and not(sel(1)) and (sel(0));
	outp(6) <= inpt and (sel(2)) and (sel(1)) and not(sel(0));
	outp(7) <= inpt and (sel(2)) and (sel(1)) and (sel(0));

END TypeArchitecture;

// VHDL entity dmux, as the project stores it:
LIBRARY ieee;
USE ieee.std_logic_1164.all;

ENTITY dmux IS
  PORT (
  	inpt: in std_logic;
	sel: in std_logic_vector(2 downto 0);
  	outp: out std_logic_vector(7 downto 0)
    );
END dmux;

--------------------------------------------------------------------------------
--Complete your VHDL description below
--------------------------------------------------------------------------------

ARCHITECTURE TypeArchitecture OF dmux IS

BEGIN

	outp(0) <= inpt and not(sel(2)) and not(sel(1)) and not(sel(0));
	outp(1) <= inpt and not(sel(2)) and not(sel(1)) and (sel(0));
	outp(2) <= inpt and not(sel(2)) and (sel(1)) and not(sel(0));
	outp(3) <= inpt and not(sel(2)) and (sel(1)) and (sel(0));
	outp(4) <= inpt and (sel(2)) and not(sel(1)) and not(sel(0));
	outp(5) <= inpt and (sel(2)) and not(sel(1)) and (sel(0));
	outp(6) <= inpt and (sel(2)) and (sel(1)) and not(sel(0));
	outp(7) <= inpt and (sel(2)) and (sel(1)) and (sel(0));

END TypeArchitecture;
