// Logisim project mub4bw.circ as structural Verilog
module main (
  input  [7:0] in_1,
  input  [7:0] in_2,
  input  [7:0] in_3,
  input  [2:0] in_4,
  input  [7:0] in_5,
  input  [3:0] in_6,
  input  [3:0] in_7,
  input  [3:0] in_8,
  input  [3:0] in_9,
  input  [3:0] in_10,
  input  [3:0] in_11,
  input  [3:0] in_12,
  input  [3:0] in_13,
  input  [2:0] in_14,
  output [3:0] out_15
);

  mux mux_1 (.inpt(in_1), .sel(in_4));  // open: outp
  mux mux_2 (.inpt(in_2), .sel(in_4));  // open: outp
  mux mux_3 (.inpt(in_3), .sel(in_4));  // open: outp
  mux mux_4 (.inpt(in_5), .sel(in_4));  // open: outp
  mux4 mux4_1 (
    .in0(in_6), .in1(in_7), .in2(in_8), .in3(in_9), .in4(in_10), .in5(in_11), .in6(in_12), .in7(in_13),
    .sel(in_14), .outp(out_15));
endmodule

// VHDL entity mux, as the project stores it:
LIBRARY ieee;
USE ieee.std_logic_1164.all;

ENTITY mux IS
  PORT (
	inpt: in std_logic_vector(7 downto 0);
	sel: in std_logic_vector(2 downto 0);
	outp: out std_logic
    );
END mux;

ARCHITECTURE TypeArchitecture OF mux IS

BEGIN
--	with sel select outp <=
--		inpt(0) when "000";

	outp <= inpt(0) when sel = "000" else
		inpt(1) when sel = "001" else
	 	inpt(2) when sel = "010" else 
	 	inpt(3) when sel = "011" else
	 	inpt(4) when sel = "100" else
	 	inpt(5) when sel = "101" else
	 	inpt(6) when sel = "110" else
	 	inpt(7) when sel = "111";

END TypeArchitecture;

// VHDL entity mux4, as the project stores it:
--------------------------------------------------------------------------------
-- Project :
-- File    :
-- Autor   :
-- Date    :
--
--------------------------------------------------------------------------------
-- Description :
--
--------------------------------------------------------------------------------

LIBRARY ieee;
USE ieee.std_logic_1164.all;

ENTITY mux4 IS
  PORT (
  	in0: in std_logic_vector(3 downto 0);
  	in1: in std_logic_vector(3 downto 0);
  	in2: in std_logic_vector(3 downto 0);
  	in3: in std_logic_vector(3 downto 0);
  	in4: in std_logic_vector(3 downto 0);
  	in5: in std_logic_vector(3 downto 0);
  	in6: in std_logic_vector(3 downto 0);
  	in7: in std_logic_vector(3 downto 0);
  	sel: in std_logic_vector(2 downto 0);
  	outp: out std_logic_vector(3 downto 0)
    );
END mux4;


ARCHITECTURE TypeArchitecture OF mux4 IS
	component mux IS
	  PORT (
		inpt: in std_logic_vector(7 downto 0);
		sel: in std_logic_vector(2 downto 0);
		outp: out std_logic
	    );
	END component;
	signal stream4: std_logic_vector(7 downto 0);
	signal stream3: std_logic_vector(7 downto 0);
	signal stream2: std_logic_vector(7 downto 0);
	signal stream1: std_logic_vector(7 downto 0);
BEGIN
	stream4 <= in7(3) & in6(3) & in5(3) & in4(3) & in3(3) & in2(3) & in1(3) & in0(3);
	stream3 <= in7(2) & in6(2) & in5(2) & in4(2) & in3(2) & in2(2) & in1(2) & in0(2);
	stream2 <= in7(1) & in6(1) & in5(1) & in4(1) & in3(1) & in2(1) & in1(1) & in0(1);
	stream1 <= in7(0) & in6(0) & in5(0) & in4(0) & in3(0) & in2(0) & in1(0) & in0(0);
	M1 : mux port map (stream4, sel, outp(3));
	M2 : mux port map (stream3, sel, outp(2));
	M3 : mux port map (stream2, sel, outp(1));
	M4 : mux port map (stream1, sel, outp(0));

END TypeArchitecture;


LIBRARY ieee;
USE ieee.std_logic_1164.all;

ENTITY mux IS
  PORT (
	inpt: in std_logic_vector(7 downto 0);
	sel: in std_logic_vector(2 downto 0);
	outp: out std_logic
    );
END mux;

ARCHITECTURE TypeArchitecture OF mux IS

BEGIN

	outp <= inpt(0) when sel = "000" else
		inpt(1) when sel = "001" else
	 	inpt(2) when sel = "010" else 
	 	inpt(3) when sel = "011" else
	 	inpt(4) when sel = "100" else
	 	inpt(5) when sel = "101" else
	 	inpt(6) when sel = "110" else
	 	inpt(7) when sel = "111";

END TypeArchitecture;
